# Fritzing sketch companion (saved by Fritzing 1.0.6)

parts:
  Part1 = Adafruit Feather M0 Adalogger [part_number="Adafruit #2796"]  # not connected
  Part2 = Adafruit FeatherWing Proto [part_number="Adafruit #2884"]
  Boost_Converter = ISL9111 Boost Converter breakout [part_number=ISL9111 package="Breakout board SOT23"]
  J1 = screw terminal, 3 pins
  C1 = Ceramic Capacitor [capacitance=10µF voltage=35V package="100 mil [THT, multilayer]"]
  J2 = male pin header, 4 pins [form="♂ (male)"]
  J3 = male pin header, 4 pins [form="♂ (male)"]
  Pressure_Sensor = mystery part, 3 pins [chip_label="Pressure Sensor"]
  R1 = Resistor [tolerance=±1% power=0.25W resistance=6.8k package=THT]
  R2 = Resistor [tolerance=±1% power=0.25W resistance=10k package=THT]
  C3 = Ceramic Capacitor [capacitance=10µF voltage=35V package="100 mil [THT, multilayer]"]
  C2 = Ceramic Capacitor [capacitance=10µF voltage=35V package="100 mil [THT, multilayer]"]
  C4 = Ceramic Capacitor [capacitance=10µF voltage=35V package="100 mil [THT, multilayer]"]
  Boost_Converter1 = ISL9111 Boost Converter breakout [part_number=ISL9111 package="Breakout board SOT23"]  # not connected
  J4 = screw terminal, 3 pins
  J5 = male pin header, 4 pins [form="♂ (male)"]
  J6 = male pin header, 4 pins [form="♂ (male)"]
  R3 = Resistor [tolerance=±1% power=0.25W resistance=6.8k package=THT]
  R4 = Resistor [tolerance=±1% power=0.25W resistance=10k package=THT]
  C5 = Ceramic Capacitor [capacitance=10µF voltage=35V package="100 mil [THT, multilayer]"]
  C6 = Ceramic Capacitor [capacitance=10µF voltage=35V package="100 mil [THT, multilayer]"]
  C7 = Ceramic Capacitor [capacitance=10µF voltage=35V package="100 mil [THT, multilayer]"]
  C8 = Ceramic Capacitor [capacitance=10µF voltage=35V package="100 mil [THT, multilayer]"]
  Part3 = Adafruit FeatherWing Proto [part_number="Adafruit #2884"]

nets (from the schematic view):
  N1: Part2.N, Part2.N$110, J2.pin1
  N2: Part2.L, Part2.N$116, Part2.N$117, J2.pin2, J3.pin2
  N3: Part2.K, Part2.N$122, J2.pin3
  N4: Part2.B, Part2.N$70, C4.0
  N5: Part2.GND, C2.0, C4.1
  N6: Part2.AREF, C2.1
  N7: Part2.N$37, C3.1
  N8: Part2.N$41, Part2.N$42, Part2.N$65, Part2.N$83, Part2.N$111, J1.pin3, C1.1, J3.pin1, Pressure_Sensor.pin1, R2.Pin_1, C3.0
  N9: Part2.N$44, Boost_Converter.OUT, C1.0, Pressure_Sensor.pin3
  N10: Part2.N$66, Part2.N$86, J1.pin2, Pressure_Sensor.pin2, R1.Pin_1
  N11: Part2.N$71, R2.Pin_0
  N12: Part2.N$78, R1.Pin_0
  N13: Part2.N$91, J1.pin1
  N14: Part2.N$121, J3.pin3
  N15: Part2.N$132, J3.pin4
  N16: Part2.N$133, J2.pin4
  N17: J4.pin1, Part3.N$96
  N18: J4.pin2, Part3.N$91
  N19: J4.pin3, Part3.N$86
  N20: J5.pin1, Part3.N$106
  N21: J5.pin2, Part3.N$111
  N22: J5.pin3, Part3.N$117
  N23: J5.pin4, Part3.N$121
  N24: J6.pin1, Part3.N$105
  N25: J6.pin2, Part3.N$112
  N26: J6.pin3, Part3.N$118
  N27: J6.pin4, Part3.N$120
  N28: R3.Pin_0, Part3.N$78
  N29: R3.Pin_1, Part3.N$66
  N30: R4.Pin_0, Part3.N$71
  N31: R4.Pin_1, Part3.N$65
  N32: C5.0, Part3.N$42
  N33: C5.1, Part3.N$37
  N34: C6.0, Part3.N$44
  N35: C6.1, Part3.N$41
  N36: C7.0, Part3.N$70
  N37: C7.1, C8.0, Part3.GND
  N38: C8.1, Part3.AREF

custom parts:
  Adafruit Feather M0 Adalogger: This is the Adafruit Feather M0 Adalogger - our take on an 'all-in-one' Cortex M0 datalogger (or data-reader) with built in USB and battery charging. Its an Adafruit Feather M0 with a microSD holder ready to rock! We have other boards in the Feather family, check'em out here At the Feather M0's heart is an ATSAMD21G18 ARM Cortex M0 processor, clocked at 48 MHz and at 3.3V logic, the same one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
  Adafruit FeatherWing Proto: This is the FeatherWing Proto - a prototyping add-on for all Feather boards. Using our Feather Stacking Headers or Feather Female Headers you can connect a FeatherWing on top or bottom of your Feather board and let the board take flight! This has a duplicate breakout for each pin on a Feather, as well as a bunch of plain grid proto holes. For GND and 3.3V, we give you a strip of connected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
  ISL9111 Boost Converter breakout: Package solution for ISL9111 boost converter, 0.8-5V->5V
